// Logisim project CalculadoraHexadecimal.circ as structural Verilog: 27 circuits, main circuit main
module main (
);

  wire _0_out, _1_out, _2_out, _3_out, _4_out, _5_out, _6_out, _7_out, _8_out, _9_out, A_out, and_1_out,
       and_2_out, B_out, button_2_out, button_3_out, button_out, C_out, CLEAR_out, D_out, display_1_a,
       display_1_b, display_1_c, display_1_d, display_1_e, display_1_f, display_1_g, display_bit_ex_1_a,
       display_bit_ex_1_b, display_bit_ex_1_c, display_bit_ex_1_d, display_bit_ex_1_e, display_bit_ex_1_f,
       display_bit_ex_1_g, displayop_1_a, displayop_1_b, displayop_1_c, displayop_1_d, displayop_1_e,
       displayop_1_f, displayop_1_g, E_out, F_out, hexa_bin_1_enable, ula_1_bit_excedente;
  wire [1:0] unidade_de_contole_1_exibir;
  wire [2:0] \bmop_1_situação ;
  wire [3:0] \banco_de_memoria_1_saída , \banco_de_memoria_2_saída , hexa_bin_1_out_17,
       mux_do_display_1_escolhido, neg_pos_1_out_5, ula_1_resultado;

  Button _0 (.out(_0_out));
  Button _4 (.out(_4_out));
  Button _8 (.out(_8_out));
  Button C (.out(C_out));
  Button button (.out(button_out));
  Button button_2 (.out(button_2_out));
  Button _1 (.out(_1_out));
  Button _5 (.out(_5_out));
  Button _9 (.out(_9_out));
  Button D (.out(D_out));
  Button CLEAR (.out(CLEAR_out));
  Button button_3 (.out(button_3_out));
  Button _3 (.out(_3_out));
  Button _2 (.out(_2_out));
  Button _6 (.out(_6_out));
  Button _7 (.out(_7_out));
  Button B (.out(B_out));
  Button A (.out(A_out));
  Button E (.out(E_out));
  Button F (.out(F_out));
  BMOP bmop_1 (
    .in_1(button_2_out), .in_2(button_out), .in_3(button_3_out), .Clear(CLEAR_out),
    .\Situação (\bmop_1_situação ));
  hexa_bin hexa_bin_1 (
    ._0(_0_out), ._1(_1_out), ._2(_2_out), ._3(_3_out), ._4(_4_out), ._5(_5_out), ._6(_6_out), ._7(_7_out),
    ._8(_8_out), ._9(_9_out), .A(A_out), .B(B_out), .C(C_out), .D(D_out), .E(E_out), .F(F_out),
    .out_17(hexa_bin_1_out_17), .Enable(hexa_bin_1_enable));
  and and_1 (and_1_out, hexa_bin_1_enable, \bmop_1_situação [2]);
  and and_2 (and_2_out, hexa_bin_1_enable, ~\bmop_1_situação [2]);  // AND_Gate
  Banco_de_memoria banco_de_memoria_1 (
    .in_2(hexa_bin_1_out_17), .Enable(and_2_out), .Clear(CLEAR_out), .\Saída (\banco_de_memoria_1_saída ));
  DISPLAYOP displayop_1 (
    .\Operação (\bmop_1_situação [1]), .A(displayop_1_a), .B(displayop_1_b), .C(displayop_1_c),
    .D(displayop_1_d), .E(displayop_1_e), .F(displayop_1_f), .G(displayop_1_g));
  _7_Segment_Display u_7_segment_display_1 (
    .g(displayop_1_g), .f(displayop_1_f), .a(displayop_1_a), .b(displayop_1_b), .e(displayop_1_e),
    .d(displayop_1_d), .c(displayop_1_c));  // open: dp
  Unidade_de_contole unidade_de_contole_1 (
    .\Operação (\bmop_1_situação [1]), .Informe_resultado(\bmop_1_situação [0]),
    .Escolheu(\bmop_1_situação [2]), .Exibir(unidade_de_contole_1_exibir));  // open: Seletor
  Banco_de_memoria banco_de_memoria_2 (
    .in_2(hexa_bin_1_out_17), .Enable(and_1_out), .Clear(CLEAR_out), .\Saída (\banco_de_memoria_2_saída ));
  ULA ula_1 (
    .A(\banco_de_memoria_1_saída ), .B(\banco_de_memoria_2_saída ), .\Operação (\bmop_1_situação [1]),
    .Resultado(ula_1_resultado), .Bit_Excedente(ula_1_bit_excedente));
  MUX_do_display mux_do_display_1 (
    .A(\banco_de_memoria_1_saída ), .B(\banco_de_memoria_2_saída ), .Resultado(ula_1_resultado),
    .Escolha(unidade_de_contole_1_exibir), .Escolhido(mux_do_display_1_escolhido));
  DISPLAY_BIT_EX display_bit_ex_1 (
    .in_1(\bmop_1_situação [1]), .in_2(\bmop_1_situação [0]), .in_3(ula_1_bit_excedente),
    .A(display_bit_ex_1_a), .B(display_bit_ex_1_b), .C(display_bit_ex_1_c), .D(display_bit_ex_1_d),
    .E(display_bit_ex_1_e), .F(display_bit_ex_1_f), .G(display_bit_ex_1_g));
  _7_Segment_Display u_7_segment_display_2 (
    .g(display_bit_ex_1_g), .f(display_bit_ex_1_f), .a(display_bit_ex_1_a), .b(display_bit_ex_1_b),
    .e(display_bit_ex_1_e), .d(display_bit_ex_1_d), .c(display_bit_ex_1_c));  // open: dp
  NEG__POS neg_pos_1 (
    .in_1(ula_1_bit_excedente), .in_2(\bmop_1_situação [1]), .in_3(\bmop_1_situação [0]),
    .Resultado(mux_do_display_1_escolhido), .out_5(neg_pos_1_out_5));
  DISPLAY display_1 (
    .in_1(neg_pos_1_out_5), .A(display_1_a), .B(display_1_b), .C(display_1_c), .D(display_1_d),
    .E(display_1_e), .F(display_1_f), .G(display_1_g));
  _7_Segment_Display u_7_segment_display_3 (
    .g(display_1_g), .f(display_1_f), .a(display_1_a), .b(display_1_b), .e(display_1_e), .d(display_1_d),
    .c(display_1_c));  // open: dp
endmodule

// hexa-bin
module hexa_bin (
  input  _0,
  input  _1,
  input  _2,
  input  _3,
  input  _4,
  input  _5,
  input  _6,
  input  _7,
  input  _8,
  input  _9,
  input  A,
  input  B,
  input  C,
  input  D,
  input  E,
  input  F,
  output [3:0] out_17,
  output Enable
);

  or S1 (out_17[3], _8, _9, A, B, C, D, E, F);
  or S2 (out_17[2], _4, _5, _6, _7, C, D, E, F);
  or S3 (out_17[1], _2, _3, _6, _7, A, B, E, F);
  or S4 (out_17[0], _1, _3, _5, _7, _9, B, D, F);
  or or_1 (Enable, _0, _1, _2, _3, _4, _5, _6, _7, _8, _9, A, B, C, D, E, F);
endmodule

// D
module Flip_Flop_D (
  input  Preset,
  input  Valor,
  input  Enable,
  input  Clear,
  output Q,
  output Q_Negado
);

  wire nand_1_out, nand_2_out;

  nand nand_1 (nand_1_out, Valor, Enable, Q_Negado);
  nand nand_2 (nand_2_out, Q, Enable, ~Valor);  // NAND_Gate
  nand nand_3 (Q, Preset, nand_1_out, Q_Negado);
  nand nand_4 (Q_Negado, Q, nand_2_out, Clear);
endmodule

// OP
module BMOP (
  input  in_1,
  input  in_2,
  input  in_3,
  input  Clear,
  output [2:0] \Situação 
);

  wire and_1_out, Ebable_out, Escolha_out, not_1_out, not_2_out, not_3_out;

  or Ebable (Ebable_out, in_1, in_2);
  or Escolha (Escolha_out, in_1, in_2);
  and and_1 (and_1_out, in_1, ~in_2);  // AND_Gate
  not not_1 (not_1_out, in_3);
  not not_2 (not_2_out, not_1_out);
  Flip_Flop_D flip_flop_d_1 (
    .Valor(Escolha_out), .Enable(Ebable_out), .Preset(1'b1), .Clear(not_3_out), .Q(\Situação [2]));  // open: Q_Negado
  Flip_Flop_D flip_flop_d_2 (
    .Valor(and_1_out), .Enable(Ebable_out), .Preset(1'b1), .Clear(not_3_out), .Q(\Situação [1]));  // open: Q_Negado
  not not_3 (not_3_out, Clear);
  Flip_Flop_D flip_flop_d_3 (
    .Valor(not_2_out), .Enable(in_3), .Preset(1'b1), .Clear(not_3_out), .Q(\Situação [0]));  // open: Q_Negado
endmodule

// UC
module Unidade_de_contole (
  input  \Operação ,
  input  Informe_resultado,
  input  Escolheu,
  output Seletor,
  output [1:0] Exibir
);

  and and_1 (Seletor, \Operação , Informe_resultado);
  and and_2 (Exibir[1], Informe_resultado, Escolheu);
  and and_3 (Exibir[0], ~Informe_resultado, Escolheu);  // AND_Gate
endmodule

// MB
module Banco_de_memoria (
  input  Enable,
  input  [3:0] in_2,
  input  Clear,
  output [3:0] \Saída 
);

  wire not_3_out;
  wire [3:0] not_1_out, not_2_out;

  assign not_1_out = ~in_2;  // NOT_Gate not_1, 4 bits wide
  assign not_2_out = ~not_1_out;  // NOT_Gate not_2, 4 bits wide
  Flip_Flop_D flip_flop_d_1 (
    .Valor(not_2_out[0]), .Enable(Enable), .Preset(1'b1), .Clear(not_3_out), .Q(\Saída [0]));  // open: Q_Negado
  Flip_Flop_D flip_flop_d_2 (
    .Valor(not_2_out[1]), .Enable(Enable), .Preset(1'b1), .Clear(not_3_out), .Q(\Saída [1]));  // open: Q_Negado
  Flip_Flop_D flip_flop_d_3 (
    .Valor(not_2_out[2]), .Enable(Enable), .Preset(1'b1), .Clear(not_3_out), .Q(\Saída [2]));  // open: Q_Negado
  Flip_Flop_D flip_flop_d_4 (
    .Valor(not_2_out[3]), .Enable(Enable), .Preset(1'b1), .Clear(not_3_out), .Q(\Saída [3]));  // open: Q_Negado
  not not_3 (not_3_out, Clear);

  // Notes on the sheet:
  //   Preset
endmodule

// meio
module Meio_somador (
  input  A,
  input  B,
  output Vai_1,
  output \Saída 
);

  and and_1 (Vai_1, A, B);
  xor xor_1 (\Saída , A, B);
endmodule

module Somador (
  input  A,
  input  B,
  input  Vem_1,
  output \Saída ,
  output Vai_1
);

  wire and_1_out, and_2_out, and_3_out, xor_1_out;

  xor xor_1 (xor_1_out, A, B);
  and and_1 (and_1_out, A, B);
  and and_2 (and_2_out, B, Vem_1);
  and and_3 (and_3_out, A, Vem_1);
  xor xor_2 (\Saída , Vem_1, xor_1_out);
  or or_1 (Vai_1, and_1_out, and_2_out, and_3_out);
endmodule

// nega
module Negar_num (
  input  [3:0] B,
  output [3:0] Negativo
);

  wire meio_somador_1_vai_1, not_1_out, not_2_out, not_3_out, not_4_out, somador_1_vai_1, somador_2_vai_1;

  not not_1 (not_1_out, B[0]);
  not not_2 (not_2_out, B[1]);
  not not_3 (not_3_out, B[2]);
  not not_4 (not_4_out, B[3]);
  Meio_somador meio_somador_1 (.A(not_1_out), .B(1'b1), .Vai_1(meio_somador_1_vai_1), .\Saída (Negativo[0]));
  Somador somador_1 (
    .A(not_2_out), .B(1'b0), .Vem_1(meio_somador_1_vai_1), .\Saída (Negativo[1]), .Vai_1(somador_1_vai_1));
  Somador somador_2 (.A(not_3_out), .B(1'b0), .Vem_1(somador_1_vai_1), .\Saída (Negativo[2]), .Vai_1(somador_2_vai_1));
  Somador somador_3 (.A(not_4_out), .B(1'b0), .Vem_1(somador_2_vai_1), .\Saída (Negativo[3]));  // open: Vai_1
endmodule

module MUX (
  input  in_1,
  input  in_2,
  input  in_3,
  output \Saída 
);

  wire and_1_out, and_2_out;

  and and_1 (and_1_out, ~in_3, in_1);  // AND_Gate
  and and_2 (and_2_out, in_3, in_2);
  or or_1 (\Saída , and_1_out, and_2_out);
endmodule

module escolha (
  input  in_1,
  input  [3:0] in_2,
  input  [3:0] in_3,
  output [3:0] out_4
);

  MUX mux_1 (.in_1(in_2[0]), .in_2(in_3[0]), .in_3(in_1), .\Saída (out_4[0]));
  MUX mux_2 (.in_1(in_2[1]), .in_2(in_3[1]), .in_3(in_1), .\Saída (out_4[1]));
  MUX mux_3 (.in_1(in_2[2]), .in_2(in_3[2]), .in_3(in_1), .\Saída (out_4[2]));
  MUX mux_4 (.in_1(in_2[3]), .in_2(in_3[3]), .in_3(in_1), .\Saída (out_4[3]));
endmodule

module soma (
  input  [3:0] in_1,
  input  [3:0] in_2,
  output [3:0] \Saída ,
  output Bit_Excedente
);

  wire meio_somador_1_vai_1, somador_1_vai_1, somador_2_vai_1;

  Meio_somador meio_somador_1 (.A(in_1[0]), .B(in_2[0]), .Vai_1(meio_somador_1_vai_1), .\Saída (\Saída [0]));
  Somador somador_1 (
    .A(in_1[1]), .B(in_2[1]), .Vem_1(meio_somador_1_vai_1), .\Saída (\Saída [1]), .Vai_1(somador_1_vai_1));
  Somador somador_2 (.A(in_1[2]), .B(in_2[2]), .Vem_1(somador_1_vai_1), .\Saída (\Saída [2]), .Vai_1(somador_2_vai_1));
  Somador somador_3 (.A(in_1[3]), .B(in_2[3]), .Vem_1(somador_2_vai_1), .\Saída (\Saída [3]), .Vai_1(Bit_Excedente));
endmodule

module ULA (
  input  \Operação ,
  input  [3:0] A,
  input  [3:0] B,
  output [3:0] Resultado,
  output Bit_Excedente
);

  wire [3:0] escolha_1_out_4, negar_num_1_negativo;

  Negar_num negar_num_1 (.B(B), .Negativo(negar_num_1_negativo));
  escolha escolha_1 (.in_2(B), .in_3(negar_num_1_negativo), .in_1(\Operação ), .out_4(escolha_1_out_4));
  soma soma_1 (.in_1(A), .in_2(escolha_1_out_4), .Bit_Excedente(Bit_Excedente), .\Saída (Resultado));
endmodule

module mux_2_bits (
  input  in_1,
  input  in_2,
  input  in_3,
  input  in_4,
  input  in_5,
  output \Saída 
);

  wire and_1_out, and_2_out, and_3_out;

  and and_1 (and_1_out, ~in_4, ~in_5, in_1);  // AND_Gate
  and and_2 (and_2_out, ~in_4, in_5, in_2);  // AND_Gate
  and and_3 (and_3_out, in_4, ~in_5, in_3);  // AND_Gate
  or or_1 (\Saída , and_1_out, and_2_out, and_3_out);
endmodule

// MUXDIS
module MUX_do_display (
  input  [1:0] Escolha,
  input  [3:0] A,
  input  [3:0] B,
  input  [3:0] Resultado,
  output [3:0] Escolhido
);

  mux_2_bits mux_2_bits_1 (
    .in_1(A[0]), .in_2(B[0]), .in_3(Resultado[0]), .in_4(Escolha[1]), .in_5(Escolha[0]),
    .\Saída (Escolhido[0]));
  mux_2_bits mux_2_bits_2 (
    .in_1(A[1]), .in_2(B[1]), .in_3(Resultado[1]), .in_4(Escolha[1]), .in_5(Escolha[0]),
    .\Saída (Escolhido[1]));
  mux_2_bits mux_2_bits_3 (
    .in_1(A[2]), .in_2(B[2]), .in_3(Resultado[2]), .in_4(Escolha[1]), .in_5(Escolha[0]),
    .\Saída (Escolhido[2]));
  mux_2_bits mux_2_bits_4 (
    .in_1(A[3]), .in_2(B[3]), .in_3(Resultado[3]), .in_4(Escolha[1]), .in_5(Escolha[0]),
    .\Saída (Escolhido[3]));
endmodule

module NEG__POS (
  input  in_1,
  input  in_2,
  input  in_3,
  input  [3:0] Resultado,
  output [3:0] out_5
);

  wire and_1_out;
  wire [3:0] negar_num_1_negativo;

  and and_1 (and_1_out, ~in_1, in_3, in_2);  // AND_Gate
  Negar_num negar_num_1 (.B(Resultado), .Negativo(negar_num_1_negativo));
  escolha escolha_1 (.in_2(Resultado), .in_3(negar_num_1_negativo), .in_1(and_1_out), .out_4(out_5));
endmodule

// OPERAÇÃO
module DISPLAYOP (
  input  \Operação ,
  output A,
  output B,
  output C,
  output D,
  output E,
  output F,
  output G
);

  nand nand_1 (A, \Operação , 1'b1);

  assign B = A;
  assign C = 1'b0;
  assign D = 1'b0;
  assign E = A;
  assign F = A;
  assign G = 1'b1;
endmodule

module DISPLAY_BIT_EX (
  input  in_1,
  input  in_2,
  input  in_3,
  output A,
  output B,
  output C,
  output D,
  output E,
  output F,
  output G
);

  wire and_1_out, and_2_out;

  and and_1 (and_1_out, in_1, in_2);
  and and_2 (and_2_out, in_2, in_3);
  xnor xnor_1 (A, and_1_out, and_2_out);
  or or_1 (B, ~and_1_out, and_2_out);  // OR_Gate
  and and_3 (G, and_1_out, ~and_2_out);  // AND_Gate

  assign C = B;
  assign D = A;
  assign E = A;
  assign F = A;
endmodule

module A (
  input  S1,
  input  S2,
  input  S3,
  input  S4,
  output A
);

  wire and_1_out, and_2_out, and_3_out, and_4_out, and_5_out, and_6_out;

  and and_1 (and_1_out, S1, ~S4);  // AND_Gate
  and and_2 (and_2_out, ~S2, ~S4);  // AND_Gate
  and and_3 (and_3_out, ~S1, S3);  // AND_Gate
  and and_4 (and_4_out, S2, S3);
  and and_5 (and_5_out, ~S1, S2, S4);  // AND_Gate
  and and_6 (and_6_out, S1, ~S2, ~S3);  // AND_Gate
  or or_1 (A, and_1_out, and_2_out, and_3_out, and_4_out, and_5_out, and_6_out);
endmodule

module B (
  input  S1,
  input  S2,
  input  S3,
  input  S4,
  output B
);

  wire and_1_out, and_2_out, and_3_out, and_4_out, and_5_out;

  and and_1 (and_1_out, ~S1, ~S2);  // AND_Gate
  and and_2 (and_2_out, ~S2, ~S4);  // AND_Gate
  and and_3 (and_3_out, ~S1, ~S3, ~S4);  // AND_Gate
  and and_4 (and_4_out, ~S1, S3, S4);  // AND_Gate
  and and_5 (and_5_out, S1, ~S3, S4);  // AND_Gate
  or or_1 (B, and_1_out, and_2_out, and_3_out, and_4_out, and_5_out);
endmodule

module C (
  input  S1,
  input  S2,
  input  S3,
  input  S4,
  output C
);

  wire and_1_out, and_2_out, and_3_out, xor_1_out;

  xor xor_1 (xor_1_out, S1, S2);
  and and_1 (and_1_out, ~S1, S4);  // AND_Gate
  and and_2 (and_2_out, ~S3, S4);  // AND_Gate
  and and_3 (and_3_out, ~S1, ~S3);  // AND_Gate
  or or_1 (C, xor_1_out, and_1_out, and_2_out, and_3_out);
endmodule

module D (
  input  S1,
  input  S2,
  input  S3,
  input  S4,
  output D
);

  wire and_1_out, and_2_out, and_3_out, and_4_out, and_5_out;

  and and_1 (and_1_out, S1, ~S3);  // AND_Gate
  and and_2 (and_2_out, S2, S3, ~S4);  // AND_Gate
  and and_3 (and_3_out, S2, ~S3, S4);  // AND_Gate
  and and_4 (and_4_out, ~S2, S3, S4);  // AND_Gate
  and and_5 (and_5_out, ~S1, ~S2, ~S4);  // AND_Gate
  or or_1 (D, and_1_out, and_2_out, and_3_out, and_4_out, and_5_out);
endmodule

module E (
  input  S1,
  input  S2,
  input  S3,
  input  S4,
  output E
);

  wire and_1_out, and_2_out, and_3_out, and_4_out;

  and and_1 (and_1_out, S1, S2);
  and and_2 (and_2_out, S1, S3);
  and and_3 (and_3_out, S3, ~S4);  // AND_Gate
  and and_4 (and_4_out, ~S2, ~S4);  // AND_Gate
  or or_1 (E, and_1_out, and_2_out, and_3_out, and_4_out);
endmodule

module F (
  input  S1,
  input  S2,
  input  S3,
  input  S4,
  output F
);

  wire and_1_out, and_2_out, and_3_out, and_4_out, and_5_out;

  and and_1 (and_1_out, S1, S3);
  and and_2 (and_2_out, S1, ~S2);  // AND_Gate
  and and_3 (and_3_out, S2, ~S4);  // AND_Gate
  and and_4 (and_4_out, ~S3, ~S4);  // AND_Gate
  and and_5 (and_5_out, ~S1, S2, ~S3);  // AND_Gate
  or or_1 (F, and_1_out, and_2_out, and_3_out, and_4_out, and_5_out);
endmodule

module G (
  input  S1,
  input  S2,
  input  S3,
  input  S4,
  output G
);

  wire and_1_out, and_2_out, and_3_out, and_4_out, and_5_out;

  and and_1 (and_1_out, S1, S4);
  and and_2 (and_2_out, S1, ~S2);  // AND_Gate
  and and_3 (and_3_out, ~S2, S3);  // AND_Gate
  and and_4 (and_4_out, S3, ~S4);  // AND_Gate
  and and_5 (and_5_out, ~S1, S2, ~S3);  // AND_Gate
  or or_1 (G, and_1_out, and_2_out, and_3_out, and_4_out, and_5_out);
endmodule

module DISPLAY (
  input  [3:0] in_1,
  output A,
  output B,
  output C,
  output D,
  output E,
  output F,
  output G
);

  B b_1 (.S1(in_1[3]), .S2(in_1[2]), .S3(in_1[1]), .S4(in_1[0]), .B(B));
  A a_1 (.S1(in_1[3]), .S2(in_1[2]), .S3(in_1[1]), .S4(in_1[0]), .A(A));
  C c_1 (.S1(in_1[3]), .S2(in_1[2]), .S3(in_1[1]), .S4(in_1[0]), .C(C));
  D d_1 (.S1(in_1[3]), .S2(in_1[2]), .S3(in_1[1]), .S4(in_1[0]), .D(D));
  E e_1 (.S1(in_1[3]), .S2(in_1[2]), .S3(in_1[1]), .S4(in_1[0]), .E(E));
  G g_1 (.S1(in_1[3]), .S2(in_1[2]), .S3(in_1[1]), .S4(in_1[0]), .G(G));
  F f_1 (.S1(in_1[3]), .S2(in_1[2]), .S3(in_1[1]), .S4(in_1[0]), .F(F));
endmodule

module converso_Hexa_Bin (
  input  _0,
  input  _1,
  input  _2,
  input  _3,
  input  _4,
  input  _5,
  input  _6,
  input  _7,
  input  _8,
  input  _9,
  input  A,
  input  B,
  input  C,
  input  D,
  input  E,
  input  F,
  output [3:0] out_17,
  output Enable
);

  or S1 (out_17[3], _8, _9, A, B, C, D, E, F);
  or S2 (out_17[2], _4, _5, _6, _7, C, D, E, F);
  or S3 (out_17[1], _2, _3, _6, _7, A, B, E, F);
  or S4 (out_17[0], _1, _3, _5, _7, _9, B, D, F);
  or or_1 (Enable, _0, _1, _2, _3, _4, _5, _6, _7, _8, _9, A, B, C, D, E, F);
endmodule
