// Logisim project storageValuesAndOp.circ as structural Verilog: 1 circuit, main circuit main
module main (
  output \OPeração 
);

  wire _0_out, _1_out, _2_out, _3_out, _4_out, _5_out, _6_out, _7_out, and_1_out, and_2_out, button_2_out,
       button_3_out, button_out, C_out, octal_7seg_1_a, octal_7seg_1_b, octal_7seg_1_c, octal_7seg_1_d,
       octal_7seg_1_e, octal_7seg_1_f, octal_7seg_1_g, octal_7seg_2_a, octal_7seg_2_b, octal_7seg_2_c,
       octal_7seg_2_d, octal_7seg_2_e, octal_7seg_2_f, octal_7seg_2_g, octal_bin_enable_1_enable,
       registraoperacao_1_jaescolheuprimeirovalor;
  wire [2:0] mb_3bit_1_output, mb_3bit_2_output, octal_bin_enable_1_bin;

  Button button (.out(button_out));
  Button button_2 (.out(button_2_out));
  Button button_3 (.out(button_3_out));
  Button _7 (.out(_7_out));
  Button _5 (.out(_5_out));
  Button _6 (.out(_6_out));
  Button _4 (.out(_4_out));
  Button _2 (.out(_2_out));
  Button _3 (.out(_3_out));
  Button _1 (.out(_1_out));
  Button _0 (.out(_0_out));
  Button C (.out(C_out));
  Octal_Bin_enable octal_bin_enable_1 (
    ._7(_7_out), ._6(_6_out), ._5(_5_out), ._4(_4_out), ._3(_3_out), ._2(_2_out), ._1(_1_out), ._0(_0_out),
    .Enable(octal_bin_enable_1_enable), .Bin(octal_bin_enable_1_bin));
  RegistraOperacao registraoperacao_1 (
    .in_1(button_out), .in_2(button_2_out), .in_3(button_3_out), .C(C_out),
    .JaEscolheuPrimeiroValor(registraoperacao_1_jaescolheuprimeirovalor), .\Operação (\OPeração ));  // open: InformaResultado
  and and_1 (and_1_out, octal_bin_enable_1_enable, registraoperacao_1_jaescolheuprimeirovalor);
  MB_3bit mb_3bit_1 (.Input(octal_bin_enable_1_bin), .Enable(and_1_out), .Clear(C_out), .Output(mb_3bit_1_output));
  and and_2 (and_2_out, octal_bin_enable_1_enable, ~registraoperacao_1_jaescolheuprimeirovalor);  // AND_Gate
  MB_3bit mb_3bit_2 (.Input(octal_bin_enable_1_bin), .Enable(and_2_out), .Clear(C_out), .Output(mb_3bit_2_output));
  Octal_7Seg octal_7seg_1 (
    .In(mb_3bit_1_output), .a(octal_7seg_1_a), .b(octal_7seg_1_b), .c(octal_7seg_1_c), .d(octal_7seg_1_d),
    .e(octal_7seg_1_e), .f(octal_7seg_1_f), .g(octal_7seg_1_g));
  Octal_7Seg octal_7seg_2 (
    .In(mb_3bit_2_output), .a(octal_7seg_2_a), .b(octal_7seg_2_b), .c(octal_7seg_2_c), .d(octal_7seg_2_d),
    .e(octal_7seg_2_e), .f(octal_7seg_2_f), .g(octal_7seg_2_g));
  _7_Segment_Display u_7_segment_display_1 (
    .g(octal_7seg_2_g), .f(octal_7seg_2_f), .a(octal_7seg_2_a), .b(octal_7seg_2_b), .e(octal_7seg_2_e),
    .d(octal_7seg_2_d), .c(octal_7seg_2_c));  // open: dp
  _7_Segment_Display u_7_segment_display_2 (
    .g(octal_7seg_1_g), .f(octal_7seg_1_f), .a(octal_7seg_1_a), .b(octal_7seg_1_b), .e(octal_7seg_1_e),
    .d(octal_7seg_1_d), .c(octal_7seg_1_c));  // open: dp
endmodule
