// Logisim project Octal-2022.circ as structural Verilog: 3 circuits, main circuit main
module main (
  input  _7,
  input  _6,
  input  _5,
  input  _4,
  input  _3,
  input  _2,
  input  _1,
  input  _0,
  input  _7_2,
  input  _6_2,
  input  _5_2,
  input  _4_2,
  input  _3_2,
  input  _2_2,
  input  _1_2,
  input  in_16,
  input  _0_2
);

  wire and_1_out, octal_7seg_1_a, octal_7seg_1_b, octal_7seg_1_c, octal_7seg_1_d, octal_7seg_1_e,
       octal_7seg_1_f, octal_7seg_1_g, unidarit_1_out_4;
  wire [2:0] c2_1_out_2, MuX_out_4, octal_bin_1_out_9, octal_bin_2_out_9, unidarit_1_out_3;

  Octal_Bin octal_bin_1 (
    ._7(_7), ._6(_6), ._5(_5), ._4(_4), ._3(_3), ._2(_2), ._1(_1), ._0(_0), .out_9(octal_bin_1_out_9));
  Octal_Bin octal_bin_2 (
    ._7(_7_2), ._6(_6_2), ._5(_5_2), ._4(_4_2), ._3(_3_2), ._2(_2_2), ._1(_1_2), ._0(_0_2),
    .out_9(octal_bin_2_out_9));
  C2 c2_1 (.in_1(octal_bin_2_out_9), .out_2(c2_1_out_2));
  Mux_3bit MuX (.in_1(octal_bin_2_out_9), .in_2(c2_1_out_2), .in_3(in_16), .out_4(MuX_out_4));
  UnidArit unidarit_1 (.in_1(octal_bin_1_out_9), .in_2(MuX_out_4), .out_4(unidarit_1_out_4), .out_3(unidarit_1_out_3));
  and and_1 (and_1_out, unidarit_1_out_4, ~in_16);  // AND_Gate
  Octal_7Seg octal_7seg_1 (
    .In(unidarit_1_out_3), .a(octal_7seg_1_a), .b(octal_7seg_1_b), .c(octal_7seg_1_c), .d(octal_7seg_1_d),
    .e(octal_7seg_1_e), .f(octal_7seg_1_f), .g(octal_7seg_1_g));
  _7_Segment_Display u_7_segment_display_1 (.b(and_1_out), .c(and_1_out));  // open: g, f, a, e, d, dp
  _7_Segment_Display u_7_segment_display_2 (
    .g(octal_7seg_1_g), .f(octal_7seg_1_f), .a(octal_7seg_1_a), .b(octal_7seg_1_b), .e(octal_7seg_1_e),
    .d(octal_7seg_1_d), .c(octal_7seg_1_c));  // open: dp
endmodule

module Mux_3bit (
  input  [2:0] in_1,
  input  [2:0] in_2,
  input  in_3,
  output [2:0] out_4
);

  Mux_2x1 mux_2x1_1 (.A(in_1[0]), .B(in_2[0]), .Sel(in_3), .S(out_4[0]));
  Mux_2x1 mux_2x1_2 (.A(in_1[1]), .B(in_2[1]), .Sel(in_3), .S(out_4[1]));
  Mux_2x1 mux_2x1_3 (.A(in_1[2]), .B(in_2[2]), .Sel(in_3), .S(out_4[2]));
endmodule

module UnidArit (
  input  [2:0] in_1,
  input  [2:0] in_2,
  output [2:0] out_3,
  output out_4
);

  wire sum_1_ts, sum_2_ts;

  SUM sum_1 (.Te(1'b0), .A(in_1[0]), .B(in_2[0]), .S(out_3[0]), .Ts(sum_1_ts));
  SUM sum_2 (.Te(sum_1_ts), .A(in_1[1]), .B(in_2[1]), .S(out_3[1]), .Ts(sum_2_ts));
  SUM sum_3 (.Te(sum_2_ts), .A(in_1[2]), .B(in_2[2]), .S(out_3[2]), .Ts(out_4));
endmodule
