// Logisim project Octal.circ as structural Verilog: 1 circuit, main circuit v1
module v1 (
  input  OP,
  input  _7,
  input  _6,
  input  _5,
  input  _4,
  input  _3,
  input  _2,
  input  _1,
  input  _0,
  input  _7_2,
  input  _6_2,
  input  _5_2,
  input  _4_2,
  input  _3_2,
  input  _2_2,
  input  _1_2,
  input  _0_2
);

  wire and_1_out, n3bit_1_carryout, octal_7seg_1_a, octal_7seg_1_b, octal_7seg_1_c, octal_7seg_1_d,
       octal_7seg_1_e, octal_7seg_1_f, octal_7seg_1_g;
  wire [2:0] n3bit_1_s, octal_bin_1_out_9, octal_bin_2_out_9;

  Octal_Bin octal_bin_1 (
    ._7(_7), ._6(_6), ._5(_5), ._4(_4), ._3(_3), ._2(_2), ._1(_1), ._0(_0), .out_9(octal_bin_1_out_9));
  Octal_Bin octal_bin_2 (
    ._7(_7_2), ._6(_6_2), ._5(_5_2), ._4(_4_2), ._3(_3_2), ._2(_2_2), ._1(_1_2), ._0(_0_2),
    .out_9(octal_bin_2_out_9));
  _3bit u_3bit_1 (
    .A(octal_bin_1_out_9), .B(octal_bin_2_out_9), .BNeg(OP), .in_2(2'b10), .S(n3bit_1_s),
    .CarryOut(n3bit_1_carryout));
  Octal_7Seg octal_7seg_1 (
    .In(n3bit_1_s), .a(octal_7seg_1_a), .b(octal_7seg_1_b), .c(octal_7seg_1_c), .d(octal_7seg_1_d),
    .e(octal_7seg_1_e), .f(octal_7seg_1_f), .g(octal_7seg_1_g));
  and and_1 (and_1_out, ~OP, n3bit_1_carryout);  // AND_Gate
  _7_Segment_Display u_7_segment_display_1 (.b(and_1_out), .c(and_1_out));  // open: g, f, a, e, d, dp
  _7_Segment_Display u_7_segment_display_2 (
    .g(octal_7seg_1_g), .f(octal_7seg_1_f), .a(octal_7seg_1_a), .b(octal_7seg_1_b), .e(octal_7seg_1_e),
    .d(octal_7seg_1_d), .c(octal_7seg_1_c));  // open: dp

  // Notes on the sheet:
  //   Soma = 0
  //   Subtração = 1
endmodule
