// Logisim project c2_8bits.circ as structural Verilog: 1 circuit, main circuit C2
module C2 (
  input  [7:0] B,
  output [7:0] C2,
  output [7:0] NOT
);

  wire n1_2sum_1_vai_1, not_2_out, sum1bit_2_vai_1, sum1bit_3_vai_1, sum1bit_4_vai_1, sum1bit_5_vai_1,
       sum1bit_6_vai_1, sum1bit_7_vai_1;

  assign NOT = ~B;  // NOT_Gate not_1, 8 bits wide
  not not_2 (not_2_out, 1'b1);
  SUM1bit sum1bit_1 (.A(NOT[7]), .B(not_2_out), .VEM1(sum1bit_2_vai_1), .S(C2[7]));  // open: VAI_1
  SUM1bit sum1bit_2 (.A(NOT[6]), .B(not_2_out), .VAI_1(sum1bit_2_vai_1), .VEM1(sum1bit_3_vai_1), .S(C2[6]));
  SUM1bit sum1bit_3 (.A(NOT[5]), .B(not_2_out), .VAI_1(sum1bit_3_vai_1), .VEM1(sum1bit_4_vai_1), .S(C2[5]));
  SUM1bit sum1bit_4 (.A(NOT[4]), .B(not_2_out), .VAI_1(sum1bit_4_vai_1), .VEM1(sum1bit_5_vai_1), .S(C2[4]));
  SUM1bit sum1bit_5 (.A(NOT[3]), .B(not_2_out), .VAI_1(sum1bit_5_vai_1), .VEM1(sum1bit_6_vai_1), .S(C2[3]));
  SUM1bit sum1bit_6 (.A(NOT[2]), .B(not_2_out), .VAI_1(sum1bit_6_vai_1), .VEM1(sum1bit_7_vai_1), .S(C2[2]));
  SUM1bit sum1bit_7 (.A(NOT[1]), .B(not_2_out), .VAI_1(sum1bit_7_vai_1), .VEM1(n1_2sum_1_vai_1), .S(C2[1]));
  _1_2SUM u_1_2sum_1 (.A(NOT[0]), .B(1'b1), .VAI_1(n1_2sum_1_vai_1), .S(C2[0]));
endmodule
