// Logisim project dmux_8bits.circ as structural Verilog: 4 circuits, main circuit dMUX 1x2 (1bit)
// dMUX
module dMUX_1x2__1bit (
  input  OP,
  input  A,
  output S1,
  output S2
);

  and and_1 (S1, ~OP, A);  // AND_Gate
  and and_2 (S2, OP, A);
endmodule

// dMUX
module dMUX_1x4__1bit (
  input  [1:0] OP,
  input  A,
  output S1,
  output S2,
  output S3,
  output S4
);

  wire dmux_1x2_1bit_1_s1, dmux_1x2_1bit_1_s2;

  dMUX_1x2__1bit dmux_1x2_1bit_1 (.A(A), .OP(OP[1]), .S1(dmux_1x2_1bit_1_s1), .S2(dmux_1x2_1bit_1_s2));
  dMUX_1x2__1bit dmux_1x2_1bit_2 (.A(dmux_1x2_1bit_1_s1), .OP(OP[0]), .S1(S1), .S2(S2));
  dMUX_1x2__1bit dmux_1x2_1bit_3 (.A(dmux_1x2_1bit_1_s2), .OP(OP[0]), .S1(S3), .S2(S4));
endmodule

// dMUX
module dMUX_1x16__1bit (
  input  [3:0] OP,
  input  A,
  output out_3,
  output out_4,
  output out_5,
  output out_6,
  output out_7,
  output out_8,
  output out_9,
  output out_10,
  output out_11,
  output out_12,
  output out_13,
  output out_14,
  output out_15,
  output out_16,
  output out_17,
  output out_18
);

  wire dmux_1x4_1bit_1_s1, dmux_1x4_1bit_1_s2, dmux_1x4_1bit_1_s3, dmux_1x4_1bit_1_s4;

  dMUX_1x4__1bit dmux_1x4_1bit_1 (
    .A(A), .OP(OP[3:2]), .S1(dmux_1x4_1bit_1_s1), .S2(dmux_1x4_1bit_1_s2), .S3(dmux_1x4_1bit_1_s3),
    .S4(dmux_1x4_1bit_1_s4));
  dMUX_1x4__1bit dmux_1x4_1bit_2 (.A(dmux_1x4_1bit_1_s1), .OP(OP[1:0]), .S1(out_3), .S2(out_4), .S3(out_5), .S4(out_6));
  dMUX_1x4__1bit dmux_1x4_1bit_3 (
    .A(dmux_1x4_1bit_1_s2), .OP(OP[1:0]), .S1(out_7), .S2(out_8), .S3(out_9), .S4(out_10));
  dMUX_1x4__1bit dmux_1x4_1bit_4 (
    .A(dmux_1x4_1bit_1_s3), .OP(OP[1:0]), .S1(out_11), .S2(out_12), .S3(out_13), .S4(out_14));
  dMUX_1x4__1bit dmux_1x4_1bit_5 (
    .A(dmux_1x4_1bit_1_s4), .OP(OP[1:0]), .S1(out_15), .S2(out_16), .S3(out_17), .S4(out_18));
endmodule

module dMUX_4bit (
  input  [3:0] in_1,
  input  habilitaescrita
);

  dMUX_1x16__1bit dmux_1x16_1bit_1 (
    .A(habilitaescrita), .OP(in_1));  // open: out_3, out_4, out_5, out_6, out_7, out_8, out_9, out_10, out_11, out_12, out_13, out_14, out_15, out_16, out_17, out_18
endmodule
