// Logisim project memorybank.circ as structural Verilog: 2 circuits, main circuit MBeta
module MBeta (
  input  [3:0] Reg_A,
  input  [3:0] Reg_B,
  input  [3:0] Escreve_Reg,
  input  habilita_escrita,
  input  [7:0] Dado,
  input  Clear,
  output [7:0] Dado_1,
  output [7:0] Dado_2
);

  wire dmux_1x16_1bit_1_out_3, dmux_1x16_1bit_1_out_4, dmux_1x16_1bit_1_out_5, dmux_1x16_1bit_1_out_6,
       dmux_1x16_1bit_1_out_7, dmux_1x16_1bit_1_out_8, dmux_1x16_1bit_1_out_9, dmux_1x16_1bit_1_out_10,
       dmux_1x16_1bit_1_out_11, dmux_1x16_1bit_1_out_12, dmux_1x16_1bit_1_out_13, dmux_1x16_1bit_1_out_14,
       dmux_1x16_1bit_1_out_15, dmux_1x16_1bit_1_out_16, dmux_1x16_1bit_1_out_17, dmux_1x16_1bit_1_out_18;
  wire [7:0] d_113_q, d_114_q, d_115_q, d_116_q, d_117_q, d_118_q, d_119_q, d_120_q, d_121_q, d_122_q,
       d_123_q, d_124_q, d_125_q, d_126_q, d_127_q, d_128_q;

  dMUX_1x16__1bit dmux_1x16_1bit_1 (
    .A(habilita_escrita), .OP(Escreve_Reg), .out_3(dmux_1x16_1bit_1_out_3), .out_4(dmux_1x16_1bit_1_out_4),
    .out_5(dmux_1x16_1bit_1_out_5), .out_6(dmux_1x16_1bit_1_out_6), .out_7(dmux_1x16_1bit_1_out_7),
    .out_8(dmux_1x16_1bit_1_out_8), .out_9(dmux_1x16_1bit_1_out_9), .out_10(dmux_1x16_1bit_1_out_10),
    .out_11(dmux_1x16_1bit_1_out_11), .out_12(dmux_1x16_1bit_1_out_12), .out_13(dmux_1x16_1bit_1_out_13),
    .out_14(dmux_1x16_1bit_1_out_14), .out_15(dmux_1x16_1bit_1_out_15), .out_16(dmux_1x16_1bit_1_out_16),
    .out_17(dmux_1x16_1bit_1_out_17), .out_18(dmux_1x16_1bit_1_out_18));
  D d_1 (.D(Dado[7]), .CK(dmux_1x16_1bit_1_out_3), .PRESET(1'b1), .CLEAR(Clear), .Q(d_113_q[7]));  // open: nQ
  D d_2 (.D(Dado[7]), .CK(dmux_1x16_1bit_1_out_4), .PRESET(1'b1), .CLEAR(Clear), .Q(d_114_q[7]));  // open: nQ
  D d_3 (.D(Dado[7]), .CK(dmux_1x16_1bit_1_out_5), .PRESET(1'b1), .CLEAR(Clear), .Q(d_115_q[7]));  // open: nQ
  D d_4 (.D(Dado[7]), .CK(dmux_1x16_1bit_1_out_6), .PRESET(1'b1), .CLEAR(Clear), .Q(d_116_q[7]));  // open: nQ
  D d_5 (.D(Dado[7]), .CK(dmux_1x16_1bit_1_out_7), .PRESET(1'b1), .CLEAR(Clear), .Q(d_117_q[7]));  // open: nQ
  D d_6 (.D(Dado[7]), .CK(dmux_1x16_1bit_1_out_8), .PRESET(1'b1), .CLEAR(Clear), .Q(d_118_q[7]));  // open: nQ
  D d_7 (.D(Dado[7]), .CK(dmux_1x16_1bit_1_out_9), .PRESET(1'b1), .CLEAR(Clear), .Q(d_119_q[7]));  // open: nQ
  D d_8 (.D(Dado[7]), .CK(dmux_1x16_1bit_1_out_10), .PRESET(1'b1), .CLEAR(Clear), .Q(d_120_q[7]));  // open: nQ
  D d_9 (.D(Dado[7]), .CK(dmux_1x16_1bit_1_out_11), .PRESET(1'b1), .CLEAR(Clear), .Q(d_121_q[7]));  // open: nQ
  D d_10 (.D(Dado[7]), .CK(dmux_1x16_1bit_1_out_12), .PRESET(1'b1), .CLEAR(Clear), .Q(d_122_q[7]));  // open: nQ
  D d_11 (.D(Dado[7]), .CK(dmux_1x16_1bit_1_out_13), .PRESET(1'b1), .CLEAR(Clear), .Q(d_123_q[7]));  // open: nQ
  D d_12 (.D(Dado[7]), .CK(dmux_1x16_1bit_1_out_14), .PRESET(1'b1), .CLEAR(Clear), .Q(d_124_q[7]));  // open: nQ
  D d_13 (.D(Dado[7]), .CK(dmux_1x16_1bit_1_out_15), .PRESET(1'b1), .CLEAR(Clear), .Q(d_125_q[7]));  // open: nQ
  D d_14 (.D(Dado[7]), .CK(dmux_1x16_1bit_1_out_16), .PRESET(1'b1), .CLEAR(Clear), .Q(d_126_q[7]));  // open: nQ
  D d_15 (.D(Dado[7]), .CK(dmux_1x16_1bit_1_out_17), .PRESET(1'b1), .CLEAR(Clear), .Q(d_127_q[7]));  // open: nQ
  D d_16 (.D(Dado[7]), .CK(dmux_1x16_1bit_1_out_18), .PRESET(1'b1), .CLEAR(Clear), .Q(d_128_q[7]));  // open: nQ
  D d_17 (.D(Dado[6]), .CK(dmux_1x16_1bit_1_out_3), .PRESET(1'b1), .CLEAR(Clear), .Q(d_113_q[6]));  // open: nQ
  D d_18 (.D(Dado[6]), .CK(dmux_1x16_1bit_1_out_4), .PRESET(1'b1), .CLEAR(Clear), .Q(d_114_q[6]));  // open: nQ
  D d_19 (.D(Dado[6]), .CK(dmux_1x16_1bit_1_out_5), .PRESET(1'b1), .CLEAR(Clear), .Q(d_115_q[6]));  // open: nQ
  D d_20 (.D(Dado[6]), .CK(dmux_1x16_1bit_1_out_6), .PRESET(1'b1), .CLEAR(Clear), .Q(d_116_q[6]));  // open: nQ
  D d_21 (.D(Dado[6]), .CK(dmux_1x16_1bit_1_out_7), .PRESET(1'b1), .CLEAR(Clear), .Q(d_117_q[6]));  // open: nQ
  D d_22 (.D(Dado[6]), .CK(dmux_1x16_1bit_1_out_8), .PRESET(1'b1), .CLEAR(Clear), .Q(d_118_q[6]));  // open: nQ
  D d_23 (.D(Dado[6]), .CK(dmux_1x16_1bit_1_out_9), .PRESET(1'b1), .CLEAR(Clear), .Q(d_119_q[6]));  // open: nQ
  D d_24 (.D(Dado[6]), .CK(dmux_1x16_1bit_1_out_10), .PRESET(1'b1), .CLEAR(Clear), .Q(d_120_q[6]));  // open: nQ
  D d_25 (.D(Dado[6]), .CK(dmux_1x16_1bit_1_out_11), .PRESET(1'b1), .CLEAR(Clear), .Q(d_121_q[6]));  // open: nQ
  D d_26 (.D(Dado[6]), .CK(dmux_1x16_1bit_1_out_12), .PRESET(1'b1), .CLEAR(Clear), .Q(d_122_q[6]));  // open: nQ
  D d_27 (.D(Dado[6]), .CK(dmux_1x16_1bit_1_out_13), .PRESET(1'b1), .CLEAR(Clear), .Q(d_123_q[6]));  // open: nQ
  D d_28 (.D(Dado[6]), .CK(dmux_1x16_1bit_1_out_14), .PRESET(1'b1), .CLEAR(Clear), .Q(d_124_q[6]));  // open: nQ
  D d_29 (.D(Dado[6]), .CK(dmux_1x16_1bit_1_out_15), .PRESET(1'b1), .CLEAR(Clear), .Q(d_125_q[6]));  // open: nQ
  D d_30 (.D(Dado[6]), .CK(dmux_1x16_1bit_1_out_16), .PRESET(1'b1), .CLEAR(Clear), .Q(d_126_q[6]));  // open: nQ
  D d_31 (.D(Dado[6]), .CK(dmux_1x16_1bit_1_out_17), .PRESET(1'b1), .CLEAR(Clear), .Q(d_127_q[6]));  // open: nQ
  D d_32 (.D(Dado[6]), .CK(dmux_1x16_1bit_1_out_18), .PRESET(1'b1), .CLEAR(Clear), .Q(d_128_q[6]));  // open: nQ
  D d_33 (.D(Dado[5]), .CK(dmux_1x16_1bit_1_out_3), .PRESET(1'b1), .CLEAR(Clear), .Q(d_113_q[5]));  // open: nQ
  D d_34 (.D(Dado[5]), .CK(dmux_1x16_1bit_1_out_4), .PRESET(1'b1), .CLEAR(Clear), .Q(d_114_q[5]));  // open: nQ
  D d_35 (.D(Dado[5]), .CK(dmux_1x16_1bit_1_out_5), .PRESET(1'b1), .CLEAR(Clear), .Q(d_115_q[5]));  // open: nQ
  D d_36 (.D(Dado[5]), .CK(dmux_1x16_1bit_1_out_6), .PRESET(1'b1), .CLEAR(Clear), .Q(d_116_q[5]));  // open: nQ
  D d_37 (.D(Dado[5]), .CK(dmux_1x16_1bit_1_out_7), .PRESET(1'b1), .CLEAR(Clear), .Q(d_117_q[5]));  // open: nQ
  D d_38 (.D(Dado[5]), .CK(dmux_1x16_1bit_1_out_8), .PRESET(1'b1), .CLEAR(Clear), .Q(d_118_q[5]));  // open: nQ
  D d_39 (.D(Dado[5]), .CK(dmux_1x16_1bit_1_out_9), .PRESET(1'b1), .CLEAR(Clear), .Q(d_119_q[5]));  // open: nQ
  D d_40 (.D(Dado[5]), .CK(dmux_1x16_1bit_1_out_10), .PRESET(1'b1), .CLEAR(Clear), .Q(d_120_q[5]));  // open: nQ
  D d_41 (.D(Dado[5]), .CK(dmux_1x16_1bit_1_out_11), .PRESET(1'b1), .CLEAR(Clear), .Q(d_121_q[5]));  // open: nQ
  D d_42 (.D(Dado[5]), .CK(dmux_1x16_1bit_1_out_12), .PRESET(1'b1), .CLEAR(Clear), .Q(d_122_q[5]));  // open: nQ
  D d_43 (.D(Dado[5]), .CK(dmux_1x16_1bit_1_out_13), .PRESET(1'b1), .CLEAR(Clear), .Q(d_123_q[5]));  // open: nQ
  D d_44 (.D(Dado[5]), .CK(dmux_1x16_1bit_1_out_14), .PRESET(1'b1), .CLEAR(Clear), .Q(d_124_q[5]));  // open: nQ
  D d_45 (.D(Dado[5]), .CK(dmux_1x16_1bit_1_out_15), .PRESET(1'b1), .CLEAR(Clear), .Q(d_125_q[5]));  // open: nQ
  D d_46 (.D(Dado[5]), .CK(dmux_1x16_1bit_1_out_16), .PRESET(1'b1), .CLEAR(Clear), .Q(d_126_q[5]));  // open: nQ
  D d_47 (.D(Dado[5]), .CK(dmux_1x16_1bit_1_out_17), .PRESET(1'b1), .CLEAR(Clear), .Q(d_127_q[5]));  // open: nQ
  D d_48 (.D(Dado[5]), .CK(dmux_1x16_1bit_1_out_18), .PRESET(1'b1), .CLEAR(Clear), .Q(d_128_q[5]));  // open: nQ
  D d_49 (.D(Dado[4]), .CK(dmux_1x16_1bit_1_out_3), .PRESET(1'b1), .CLEAR(Clear), .Q(d_113_q[4]));  // open: nQ
  D d_50 (.D(Dado[4]), .CK(dmux_1x16_1bit_1_out_4), .PRESET(1'b1), .CLEAR(Clear), .Q(d_114_q[4]));  // open: nQ
  D d_51 (.D(Dado[4]), .CK(dmux_1x16_1bit_1_out_5), .PRESET(1'b1), .CLEAR(Clear), .Q(d_115_q[4]));  // open: nQ
  D d_52 (.D(Dado[4]), .CK(dmux_1x16_1bit_1_out_6), .PRESET(1'b1), .CLEAR(Clear), .Q(d_116_q[4]));  // open: nQ
  D d_53 (.D(Dado[4]), .CK(dmux_1x16_1bit_1_out_7), .PRESET(1'b1), .CLEAR(Clear), .Q(d_117_q[4]));  // open: nQ
  D d_54 (.D(Dado[4]), .CK(dmux_1x16_1bit_1_out_8), .PRESET(1'b1), .CLEAR(Clear), .Q(d_118_q[4]));  // open: nQ
  D d_55 (.D(Dado[4]), .CK(dmux_1x16_1bit_1_out_9), .PRESET(1'b1), .CLEAR(Clear), .Q(d_119_q[4]));  // open: nQ
  D d_56 (.D(Dado[4]), .CK(dmux_1x16_1bit_1_out_10), .PRESET(1'b1), .CLEAR(Clear), .Q(d_120_q[4]));  // open: nQ
  D d_57 (.D(Dado[4]), .CK(dmux_1x16_1bit_1_out_11), .PRESET(1'b1), .CLEAR(Clear), .Q(d_121_q[4]));  // open: nQ
  D d_58 (.D(Dado[4]), .CK(dmux_1x16_1bit_1_out_12), .PRESET(1'b1), .CLEAR(Clear), .Q(d_122_q[4]));  // open: nQ
  D d_59 (.D(Dado[4]), .CK(dmux_1x16_1bit_1_out_13), .PRESET(1'b1), .CLEAR(Clear), .Q(d_123_q[4]));  // open: nQ
  D d_60 (.D(Dado[4]), .CK(dmux_1x16_1bit_1_out_14), .PRESET(1'b1), .CLEAR(Clear), .Q(d_124_q[4]));  // open: nQ
  D d_61 (.D(Dado[4]), .CK(dmux_1x16_1bit_1_out_15), .PRESET(1'b1), .CLEAR(Clear), .Q(d_125_q[4]));  // open: nQ
  D d_62 (.D(Dado[4]), .CK(dmux_1x16_1bit_1_out_16), .PRESET(1'b1), .CLEAR(Clear), .Q(d_126_q[4]));  // open: nQ
  D d_63 (.D(Dado[4]), .CK(dmux_1x16_1bit_1_out_17), .PRESET(1'b1), .CLEAR(Clear), .Q(d_127_q[4]));  // open: nQ
  D d_64 (.D(Dado[4]), .CK(dmux_1x16_1bit_1_out_18), .PRESET(1'b1), .CLEAR(Clear), .Q(d_128_q[4]));  // open: nQ
  D d_65 (.D(Dado[3]), .CK(dmux_1x16_1bit_1_out_3), .PRESET(1'b1), .CLEAR(Clear), .Q(d_113_q[3]));  // open: nQ
  D d_66 (.D(Dado[3]), .CK(dmux_1x16_1bit_1_out_4), .PRESET(1'b1), .CLEAR(Clear), .Q(d_114_q[3]));  // open: nQ
  D d_67 (.D(Dado[3]), .CK(dmux_1x16_1bit_1_out_5), .PRESET(1'b1), .CLEAR(Clear), .Q(d_115_q[3]));  // open: nQ
  D d_68 (.D(Dado[3]), .CK(dmux_1x16_1bit_1_out_6), .PRESET(1'b1), .CLEAR(Clear), .Q(d_116_q[3]));  // open: nQ
  D d_69 (.D(Dado[3]), .CK(dmux_1x16_1bit_1_out_7), .PRESET(1'b1), .CLEAR(Clear), .Q(d_117_q[3]));  // open: nQ
  D d_70 (.D(Dado[3]), .CK(dmux_1x16_1bit_1_out_8), .PRESET(1'b1), .CLEAR(Clear), .Q(d_118_q[3]));  // open: nQ
  D d_71 (.D(Dado[3]), .CK(dmux_1x16_1bit_1_out_9), .PRESET(1'b1), .CLEAR(Clear), .Q(d_119_q[3]));  // open: nQ
  D d_72 (.D(Dado[3]), .CK(dmux_1x16_1bit_1_out_10), .PRESET(1'b1), .CLEAR(Clear), .Q(d_120_q[3]));  // open: nQ
  D d_73 (.D(Dado[3]), .CK(dmux_1x16_1bit_1_out_11), .PRESET(1'b1), .CLEAR(Clear), .Q(d_121_q[3]));  // open: nQ
  D d_74 (.D(Dado[3]), .CK(dmux_1x16_1bit_1_out_12), .PRESET(1'b1), .CLEAR(Clear), .Q(d_122_q[3]));  // open: nQ
  D d_75 (.D(Dado[3]), .CK(dmux_1x16_1bit_1_out_13), .PRESET(1'b1), .CLEAR(Clear), .Q(d_123_q[3]));  // open: nQ
  D d_76 (.D(Dado[3]), .CK(dmux_1x16_1bit_1_out_14), .PRESET(1'b1), .CLEAR(Clear), .Q(d_124_q[3]));  // open: nQ
  D d_77 (.D(Dado[3]), .CK(dmux_1x16_1bit_1_out_15), .PRESET(1'b1), .CLEAR(Clear), .Q(d_125_q[3]));  // open: nQ
  D d_78 (.D(Dado[3]), .CK(dmux_1x16_1bit_1_out_16), .PRESET(1'b1), .CLEAR(Clear), .Q(d_126_q[3]));  // open: nQ
  D d_79 (.D(Dado[3]), .CK(dmux_1x16_1bit_1_out_17), .PRESET(1'b1), .CLEAR(Clear), .Q(d_127_q[3]));  // open: nQ
  D d_80 (.D(Dado[3]), .CK(dmux_1x16_1bit_1_out_18), .PRESET(1'b1), .CLEAR(Clear), .Q(d_128_q[3]));  // open: nQ
  D d_81 (.D(Dado[2]), .CK(dmux_1x16_1bit_1_out_3), .PRESET(1'b1), .CLEAR(Clear), .Q(d_113_q[2]));  // open: nQ
  D d_82 (.D(Dado[2]), .CK(dmux_1x16_1bit_1_out_4), .PRESET(1'b1), .CLEAR(Clear), .Q(d_114_q[2]));  // open: nQ
  D d_83 (.D(Dado[1]), .CK(dmux_1x16_1bit_1_out_4), .PRESET(1'b1), .CLEAR(Clear), .Q(d_114_q[1]));  // open: nQ
  D d_84 (.D(Dado[2]), .CK(dmux_1x16_1bit_1_out_5), .PRESET(1'b1), .CLEAR(Clear), .Q(d_115_q[2]));  // open: nQ
  D d_85 (.D(Dado[1]), .CK(dmux_1x16_1bit_1_out_5), .PRESET(1'b1), .CLEAR(Clear), .Q(d_115_q[1]));  // open: nQ
  D d_86 (.D(Dado[1]), .CK(dmux_1x16_1bit_1_out_6), .PRESET(1'b1), .CLEAR(Clear), .Q(d_116_q[1]));  // open: nQ
  D d_87 (.D(Dado[2]), .CK(dmux_1x16_1bit_1_out_6), .PRESET(1'b1), .CLEAR(Clear), .Q(d_116_q[2]));  // open: nQ
  D d_88 (.D(Dado[2]), .CK(dmux_1x16_1bit_1_out_7), .PRESET(1'b1), .CLEAR(Clear), .Q(d_117_q[2]));  // open: nQ
  D d_89 (.D(Dado[1]), .CK(dmux_1x16_1bit_1_out_7), .PRESET(1'b1), .CLEAR(Clear), .Q(d_117_q[1]));  // open: nQ
  D d_90 (.D(Dado[1]), .CK(dmux_1x16_1bit_1_out_8), .PRESET(1'b1), .CLEAR(Clear), .Q(d_118_q[1]));  // open: nQ
  D d_91 (.D(Dado[2]), .CK(dmux_1x16_1bit_1_out_8), .PRESET(1'b1), .CLEAR(Clear), .Q(d_118_q[2]));  // open: nQ
  D d_92 (.D(Dado[1]), .CK(dmux_1x16_1bit_1_out_9), .PRESET(1'b1), .CLEAR(Clear), .Q(d_119_q[1]));  // open: nQ
  D d_93 (.D(Dado[2]), .CK(dmux_1x16_1bit_1_out_9), .PRESET(1'b1), .CLEAR(Clear), .Q(d_119_q[2]));  // open: nQ
  D d_94 (.D(Dado[2]), .CK(dmux_1x16_1bit_1_out_10), .PRESET(1'b1), .CLEAR(Clear), .Q(d_120_q[2]));  // open: nQ
  D d_95 (.D(Dado[1]), .CK(dmux_1x16_1bit_1_out_10), .PRESET(1'b1), .CLEAR(Clear), .Q(d_120_q[1]));  // open: nQ
  D d_96 (.D(Dado[1]), .CK(dmux_1x16_1bit_1_out_11), .PRESET(1'b1), .CLEAR(Clear), .Q(d_121_q[1]));  // open: nQ
  D d_97 (.D(Dado[2]), .CK(dmux_1x16_1bit_1_out_11), .PRESET(1'b1), .CLEAR(Clear), .Q(d_121_q[2]));  // open: nQ
  D d_98 (.D(Dado[1]), .CK(dmux_1x16_1bit_1_out_12), .PRESET(1'b1), .CLEAR(Clear), .Q(d_122_q[1]));  // open: nQ
  D d_99 (.D(Dado[2]), .CK(dmux_1x16_1bit_1_out_12), .PRESET(1'b1), .CLEAR(Clear), .Q(d_122_q[2]));  // open: nQ
  D d_100 (.D(Dado[2]), .CK(dmux_1x16_1bit_1_out_13), .PRESET(1'b1), .CLEAR(Clear), .Q(d_123_q[2]));  // open: nQ
  D d_101 (.D(Dado[1]), .CK(dmux_1x16_1bit_1_out_13), .PRESET(1'b1), .CLEAR(Clear), .Q(d_123_q[1]));  // open: nQ
  D d_102 (.D(Dado[1]), .CK(dmux_1x16_1bit_1_out_14), .PRESET(1'b1), .CLEAR(Clear), .Q(d_124_q[1]));  // open: nQ
  D d_103 (.D(Dado[2]), .CK(dmux_1x16_1bit_1_out_14), .PRESET(1'b1), .CLEAR(Clear), .Q(d_124_q[2]));  // open: nQ
  D d_104 (.D(Dado[1]), .CK(dmux_1x16_1bit_1_out_15), .PRESET(1'b1), .CLEAR(Clear), .Q(d_125_q[1]));  // open: nQ
  D d_105 (.D(Dado[2]), .CK(dmux_1x16_1bit_1_out_15), .PRESET(1'b1), .CLEAR(Clear), .Q(d_125_q[2]));  // open: nQ
  D d_106 (.D(Dado[2]), .CK(dmux_1x16_1bit_1_out_16), .PRESET(1'b1), .CLEAR(Clear), .Q(d_126_q[2]));  // open: nQ
  D d_107 (.D(Dado[1]), .CK(dmux_1x16_1bit_1_out_16), .PRESET(1'b1), .CLEAR(Clear), .Q(d_126_q[1]));  // open: nQ
  D d_108 (.D(Dado[2]), .CK(dmux_1x16_1bit_1_out_17), .PRESET(1'b1), .CLEAR(Clear), .Q(d_127_q[2]));  // open: nQ
  D d_109 (.D(Dado[1]), .CK(dmux_1x16_1bit_1_out_17), .PRESET(1'b1), .CLEAR(Clear), .Q(d_127_q[1]));  // open: nQ
  D d_110 (.D(Dado[1]), .CK(dmux_1x16_1bit_1_out_18), .PRESET(1'b1), .CLEAR(Clear), .Q(d_128_q[1]));  // open: nQ
  D d_111 (.D(Dado[2]), .CK(dmux_1x16_1bit_1_out_18), .PRESET(1'b1), .CLEAR(Clear), .Q(d_128_q[2]));  // open: nQ
  D d_112 (.D(Dado[1]), .CK(dmux_1x16_1bit_1_out_3), .PRESET(1'b1), .CLEAR(Clear), .Q(d_113_q[1]));  // open: nQ
  D d_113 (.D(Dado[0]), .CK(dmux_1x16_1bit_1_out_3), .PRESET(1'b1), .CLEAR(Clear), .Q(d_113_q[0]));  // open: nQ
  D d_114 (.D(Dado[0]), .CK(dmux_1x16_1bit_1_out_4), .PRESET(1'b1), .CLEAR(Clear), .Q(d_114_q[0]));  // open: nQ
  D d_115 (.D(Dado[0]), .CK(dmux_1x16_1bit_1_out_5), .PRESET(1'b1), .CLEAR(Clear), .Q(d_115_q[0]));  // open: nQ
  D d_116 (.D(Dado[0]), .CK(dmux_1x16_1bit_1_out_6), .PRESET(1'b1), .CLEAR(Clear), .Q(d_116_q[0]));  // open: nQ
  D d_117 (.D(Dado[0]), .CK(dmux_1x16_1bit_1_out_7), .PRESET(1'b1), .CLEAR(Clear), .Q(d_117_q[0]));  // open: nQ
  D d_118 (.D(Dado[0]), .CK(dmux_1x16_1bit_1_out_8), .PRESET(1'b1), .CLEAR(Clear), .Q(d_118_q[0]));  // open: nQ
  D d_119 (.D(Dado[0]), .CK(dmux_1x16_1bit_1_out_9), .PRESET(1'b1), .CLEAR(Clear), .Q(d_119_q[0]));  // open: nQ
  D d_120 (.D(Dado[0]), .CK(dmux_1x16_1bit_1_out_10), .PRESET(1'b1), .CLEAR(Clear), .Q(d_120_q[0]));  // open: nQ
  D d_121 (.D(Dado[0]), .CK(dmux_1x16_1bit_1_out_11), .PRESET(1'b1), .CLEAR(Clear), .Q(d_121_q[0]));  // open: nQ
  D d_122 (.D(Dado[0]), .CK(dmux_1x16_1bit_1_out_12), .PRESET(1'b1), .CLEAR(Clear), .Q(d_122_q[0]));  // open: nQ
  D d_123 (.D(Dado[0]), .CK(dmux_1x16_1bit_1_out_13), .PRESET(1'b1), .CLEAR(Clear), .Q(d_123_q[0]));  // open: nQ
  D d_124 (.D(Dado[0]), .CK(dmux_1x16_1bit_1_out_14), .PRESET(1'b1), .CLEAR(Clear), .Q(d_124_q[0]));  // open: nQ
  D d_125 (.D(Dado[0]), .CK(dmux_1x16_1bit_1_out_15), .PRESET(1'b1), .CLEAR(Clear), .Q(d_125_q[0]));  // open: nQ
  D d_126 (.D(Dado[0]), .CK(dmux_1x16_1bit_1_out_16), .PRESET(1'b1), .CLEAR(Clear), .Q(d_126_q[0]));  // open: nQ
  D d_127 (.D(Dado[0]), .CK(dmux_1x16_1bit_1_out_17), .PRESET(1'b1), .CLEAR(Clear), .Q(d_127_q[0]));  // open: nQ
  D d_128 (.D(Dado[0]), .CK(dmux_1x16_1bit_1_out_18), .PRESET(1'b1), .CLEAR(Clear), .Q(d_128_q[0]));  // open: nQ
  MUX16x1 mux16x1_1 (
    .A(d_113_q), .B(d_114_q), .C(d_115_q), .D(d_116_q), .E(d_117_q), .F(d_118_q), .G(d_119_q), .H(d_120_q),
    .I(d_121_q), .J(d_122_q), .K(d_123_q), .L(d_124_q), .M(d_125_q), .N(d_126_q), .O(d_127_q), .P(d_128_q),
    .OP(Reg_A), .out_18(Dado_1));
  MUX16x1 mux16x1_2 (
    .A(d_113_q), .B(d_114_q), .C(d_115_q), .D(d_116_q), .E(d_117_q), .F(d_118_q), .G(d_119_q), .H(d_120_q),
    .I(d_121_q), .J(d_122_q), .K(d_123_q), .L(d_124_q), .M(d_125_q), .N(d_126_q), .O(d_127_q), .P(d_128_q),
    .OP(Reg_B), .out_18(Dado_2));
endmodule

module teste (
  input  [3:0] Reg_A,
  input  [3:0] Reg_B,
  input  [3:0] Escreve_Reg,
  input  clock,
  input  [7:0] Dado,
  input  in_6,
  output [7:0] Dado_1,
  output [7:0] Dado_2
);

  MBeta mbeta_1 (
    .Reg_A(Reg_A), .Reg_B(Reg_B), .Escreve_Reg(Escreve_Reg), .habilita_escrita(clock), .Dado(Dado),
    .Clear(in_6), .Dado_1(Dado_1), .Dado_2(Dado_2));
endmodule
