// Logisim project mux_8bits.circ as structural Verilog: 4 circuits, main circuit MUX2x1
// MUX
module MUX2x1 (
  input  OP,
  input  [7:0] A,
  input  [7:0] B,
  output [7:0] S
);

  wire and_1_out, and_2_out, and_3_out, and_4_out, and_5_out, and_6_out, and_7_out, and_8_out, and_9_out,
       and_10_out, and_11_out, and_12_out, and_13_out, and_14_out, and_15_out, and_16_out;

  and and_1 (and_1_out, A[7], ~OP);  // AND_Gate
  and and_2 (and_2_out, B[7], OP);
  and and_3 (and_3_out, A[6], ~OP);  // AND_Gate
  and and_4 (and_4_out, B[6], OP);
  and and_5 (and_5_out, A[5], ~OP);  // AND_Gate
  and and_6 (and_6_out, B[5], OP);
  and and_7 (and_7_out, A[4], ~OP);  // AND_Gate
  and and_8 (and_8_out, B[4], OP);
  and and_9 (and_9_out, A[3], ~OP);  // AND_Gate
  and and_10 (and_10_out, B[3], OP);
  and and_11 (and_11_out, A[2], ~OP);  // AND_Gate
  and and_12 (and_12_out, B[2], OP);
  and and_13 (and_13_out, A[1], ~OP);  // AND_Gate
  and and_14 (and_14_out, B[1], OP);
  and and_15 (and_15_out, A[0], ~OP);  // AND_Gate
  and and_16 (and_16_out, B[0], OP);
  or or_1 (S[7], and_1_out, and_2_out);
  or or_2 (S[6], and_3_out, and_4_out);
  or or_3 (S[5], and_5_out, and_6_out);
  or or_4 (S[4], and_7_out, and_8_out);
  or or_5 (S[3], and_9_out, and_10_out);
  or or_6 (S[2], and_11_out, and_12_out);
  or or_7 (S[1], and_13_out, and_14_out);
  or or_8 (S[0], and_15_out, and_16_out);
endmodule

// MUX
module MUX4x1 (
  input  [1:0] in_1,
  input  [7:0] A,
  input  [7:0] B,
  input  [7:0] C,
  input  [7:0] D,
  output [7:0] out_6
);

  wire [7:0] mux2x1_1_s, mux2x1_3_s;

  MUX2x1 mux2x1_1 (.A(A), .B(B), .OP(in_1[0]), .S(mux2x1_1_s));
  MUX2x1 mux2x1_2 (.A(mux2x1_1_s), .B(mux2x1_3_s), .OP(in_1[1]), .S(out_6));
  MUX2x1 mux2x1_3 (.A(C), .B(D), .OP(in_1[0]), .S(mux2x1_3_s));
endmodule

// MUX
module MUX8x1 (
  input  [2:0] OP,
  input  [7:0] A,
  input  [7:0] B,
  input  [7:0] C,
  input  [7:0] D,
  input  [7:0] E,
  input  [7:0] F,
  input  [7:0] G,
  input  [7:0] H,
  output [7:0] S
);

  wire [7:0] mux4x1_1_out_6, mux4x1_2_out_6;

  MUX4x1 mux4x1_1 (.A(A), .B(B), .C(C), .D(D), .in_1(OP[1:0]), .out_6(mux4x1_1_out_6));
  MUX4x1 mux4x1_2 (.A(E), .B(F), .C(G), .D(H), .in_1(OP[1:0]), .out_6(mux4x1_2_out_6));
  MUX2x1 mux2x1_1 (.A(mux4x1_1_out_6), .B(mux4x1_2_out_6), .OP(OP[2]), .S(S));
endmodule

module MUX16x1 (
  input  [3:0] OP,
  input  [7:0] A,
  input  [7:0] B,
  input  [7:0] C,
  input  [7:0] D,
  input  [7:0] E,
  input  [7:0] F,
  input  [7:0] G,
  input  [7:0] H,
  input  [7:0] I,
  input  [7:0] J,
  input  [7:0] K,
  input  [7:0] L,
  input  [7:0] M,
  input  [7:0] N,
  input  [7:0] O,
  input  [7:0] P,
  output [7:0] out_18
);

  wire [7:0] mux8x1_1_s, mux8x1_2_s;

  MUX8x1 mux8x1_1 (.A(A), .B(B), .C(C), .D(D), .E(E), .F(F), .G(G), .H(H), .OP(OP[2:0]), .S(mux8x1_1_s));
  MUX8x1 mux8x1_2 (.A(I), .B(J), .C(K), .D(L), .E(M), .F(N), .G(O), .H(P), .OP(OP[2:0]), .S(mux8x1_2_s));
  MUX2x1 mux2x1_1 (.A(mux8x1_1_s), .B(mux8x1_2_s), .OP(OP[3]), .S(out_18));
endmodule
