// Logisim project sum_8bits.circ as structural Verilog: 3 circuits, main circuit 1/2SUM
module _1_2SUM (
  input  A,
  input  B,
  output S,
  output VAI_1
);

  xor xor_1 (S, A, B);
  and and_1 (VAI_1, A, B);
endmodule

module SUM1bit (
  input  A,
  input  B,
  input  VEM1,
  output S,
  output VAI_1
);

  wire and_1_out, and_2_out, and_3_out, xor_1_out;

  xor xor_1 (xor_1_out, A, B);
  and and_1 (and_1_out, A, B);
  and and_2 (and_2_out, A, VEM1);
  and and_3 (and_3_out, B, VEM1);
  xor xor_2 (S, xor_1_out, VEM1);
  or or_1 (VAI_1, and_1_out, and_2_out, and_3_out);
endmodule

module SUM8bit (
  input  [7:0] A,
  input  [7:0] B,
  output OVERFLOW,
  output [7:0] S
);

  wire n1_2sum_1_vai_1, sum1bit_2_vai_1, sum1bit_3_vai_1, sum1bit_4_vai_1, sum1bit_5_vai_1, sum1bit_6_vai_1,
       sum1bit_7_vai_1;

  SUM1bit sum1bit_1 (.A(A[7]), .B(B[7]), .VAI_1(OVERFLOW), .VEM1(sum1bit_2_vai_1), .S(S[7]));
  SUM1bit sum1bit_2 (.A(A[6]), .B(B[6]), .VAI_1(sum1bit_2_vai_1), .VEM1(sum1bit_3_vai_1), .S(S[6]));
  SUM1bit sum1bit_3 (.A(A[5]), .B(B[5]), .VAI_1(sum1bit_3_vai_1), .VEM1(sum1bit_4_vai_1), .S(S[5]));
  SUM1bit sum1bit_4 (.A(A[4]), .B(B[4]), .VAI_1(sum1bit_4_vai_1), .VEM1(sum1bit_5_vai_1), .S(S[4]));
  SUM1bit sum1bit_5 (.A(A[3]), .B(B[3]), .VAI_1(sum1bit_5_vai_1), .VEM1(sum1bit_6_vai_1), .S(S[3]));
  SUM1bit sum1bit_6 (.A(A[2]), .B(B[2]), .VAI_1(sum1bit_6_vai_1), .VEM1(sum1bit_7_vai_1), .S(S[2]));
  SUM1bit sum1bit_7 (.A(A[1]), .B(B[1]), .VAI_1(sum1bit_7_vai_1), .VEM1(n1_2sum_1_vai_1), .S(S[1]));
  _1_2SUM u_1_2sum_1 (.A(A[0]), .B(B[0]), .VAI_1(n1_2sum_1_vai_1), .S(S[0]));
endmodule
