// Logisim project ula_8bits.circ as structural Verilog: 1 circuit, main circuit ULA
module ULA (
  input  Bneg,
  input  [3:0] OP,
  input  [7:0] A,
  input  [7:0] B,
  output [7:0] S
);

  wire [7:0] AND_out, c2_1_c2, c2_1_not, equal_1_s, mux2x1_1_s, OR_out, slt8bits_1_s, sum8bit_1_s;

  MUX2x1 mux2x1_1 (.A(B), .B(c2_1_c2), .OP(Bneg), .S(mux2x1_1_s));
  C2 c2_1 (.B(B), .NOT(c2_1_not), .C2(c2_1_c2));
  SUM8bit sum8bit_1 (.A(A), .B(mux2x1_1_s), .S(sum8bit_1_s));  // open: OVERFLOW
  assign AND_out = A & mux2x1_1_s;  // AND_Gate AND, 8 bits wide
  assign OR_out = A | mux2x1_1_s;  // OR_Gate OR, 8 bits wide
  SLT8bits slt8bits_1 (.A(A), .B(mux2x1_1_s), .S(slt8bits_1_s));
  EQUAL equal_1 (.A(A), .B(mux2x1_1_s), .S(equal_1_s));
  MUX16x1 mux16x1_1 (
    .A(sum8bit_1_s), .B(AND_out), .C(OR_out), .D(slt8bits_1_s), .E(equal_1_s), .F(c2_1_not), .G({8{1'b0}}),
    .H({8{1'b0}}), .I({8{1'b0}}), .J({8{1'b0}}), .K({8{1'b0}}), .L({8{1'b0}}), .M({8{1'b0}}), .N({8{1'b0}}),
    .O({8{1'b0}}), .P({8{1'b0}}), .OP(OP), .out_18(S));
endmodule
