// Logisim project C2.circ as structural Verilog: 1 circuit, main circuit C2
// C2-3bit
module C2 (
  input  [2:0] in_1,
  output [2:0] out_2
);

  wire not_1_out, not_2_out, not_3_out, sum_1_ts, sum_2_ts;

  not not_1 (not_1_out, in_1[0]);
  not not_2 (not_2_out, in_1[1]);
  not not_3 (not_3_out, in_1[2]);
  SUM sum_1 (.Te(1'b0), .A(not_1_out), .B(1'b1), .S(out_2[0]), .Ts(sum_1_ts));
  SUM sum_2 (.Te(sum_1_ts), .A(not_2_out), .B(1'b0), .S(out_2[1]), .Ts(sum_2_ts));
  SUM sum_3 (.Te(sum_2_ts), .A(not_3_out), .B(1'b0), .S(out_2[2]));  // open: Ts
endmodule
