// Logisim project CALCAux.circ as structural Verilog: 1 circuit, main circuit RegistraOperacao
// BOp
module RegistraOperacao (
  input  in_1,
  input  in_2,
  input  in_3,
  input  C,
  output JaEscolheuPrimeiroValor,
  output \Operação ,
  output InformaResultado
);

  wire and_1_out, nor_1_out, not_1_out, not_2_out, not_3_out, not_4_out, or_1_out;

  not not_1 (not_1_out, nor_1_out);
  nor nor_1 (nor_1_out, in_2, in_1);
  or or_1 (or_1_out, in_2, in_1);
  and and_1 (and_1_out, in_1, ~in_2);  // AND_Gate
  not not_2 (not_2_out, in_3);
  not not_3 (not_3_out, not_2_out);
  D d_1 (.D(or_1_out), .Clock(not_1_out), .CLEAR(not_4_out), .PRESET(1'b1), .Q(JaEscolheuPrimeiroValor));  // open: nQ
  D d_2 (.D(and_1_out), .Clock(not_1_out), .CLEAR(not_4_out), .PRESET(1'b1), .Q(\Operação ));  // open: nQ
  D d_3 (.D(in_3), .Clock(not_3_out), .CLEAR(not_4_out), .PRESET(1'b1), .Q(InformaResultado));  // open: nQ
  not not_4 (not_4_out, C);

  // Notes on the sheet:
  //   0 = soma 1= subtração
endmodule
