// Logisim project MB.circ as structural Verilog: 1 circuit, main circuit MB 3bit
// MB
module MB_3bit (
  input  Enable,
  input  [2:0] Input,
  input  Clear,
  output [2:0] Output
);

  wire not_1_out;

  D d_1 (.D(Input[0]), .Clock(Enable), .CLEAR(not_1_out), .PRESET(1'b1), .Q(Output[0]));  // open: nQ
  D d_2 (.D(Input[1]), .Clock(Enable), .CLEAR(not_1_out), .PRESET(1'b1), .Q(Output[1]));  // open: nQ
  D d_3 (.D(Input[2]), .Clock(Enable), .CLEAR(not_1_out), .PRESET(1'b1), .Q(Output[2]));  // open: nQ
  not not_1 (not_1_out, Clear);
endmodule
