// Logisim project MUX.circ as structural Verilog: 2 circuits, main circuit Mux-2x1
// 2x1
module Mux_2x1 (
  input  Sel,
  input  A,
  input  B,
  output S
);

  wire and_1_out, and_2_out;

  and and_1 (and_1_out, A, ~Sel);  // AND_Gate
  or or_1 (S, and_1_out, and_2_out);
  and and_2 (and_2_out, B, Sel);
endmodule

module Mux_4x1 (
  input  [1:0] Sel,
  input  _0,
  input  _1,
  input  _2,
  input  _3,
  output S
);

  wire and_1_out, and_2_out, and_3_out, and_4_out;

  and and_1 (and_1_out, _0, ~Sel[1], ~Sel[0]);  // AND_Gate
  and and_2 (and_2_out, _1, ~Sel[1], Sel[0]);  // AND_Gate
  and and_3 (and_3_out, _2, Sel[1], ~Sel[0]);  // AND_Gate
  and and_4 (and_4_out, _3, Sel[1], Sel[0]);
  or or_1 (S, and_1_out, and_2_out, and_3_out, and_4_out);
endmodule
