// Logisim project OCTAL.circ as structural Verilog: 3 circuits, main circuit Octal-7Seg
module Octal_7Seg (
  input  [2:0] In,
  output a,
  output b,
  output c,
  output d,
  output e,
  output f,
  output g
);

  wire and_1_out, and_2_out, and_3_out, and_4_out, and_5_out, and_6_out, and_7_out, and_8_out, and_9_out,
       and_10_out, and_11_out, and_12_out, and_13_out, and_14_out, and_15_out, and_16_out;

  and and_1 (and_1_out, ~In[2], ~In[0]);  // AND_Gate
  and and_2 (and_2_out, In[2], In[0]);
  and and_3 (and_3_out, ~In[1], ~In[0]);  // AND_Gate
  and and_4 (and_4_out, In[1], In[0]);
  and and_5 (and_5_out, In[1], ~In[2]);  // AND_Gate
  and and_6 (and_6_out, In[1], ~In[0]);  // AND_Gate
  and and_7 (and_7_out, ~In[2], ~In[0]);  // AND_Gate
  and and_8 (and_8_out, In[2], ~In[1], In[0]);  // AND_Gate
  and and_9 (and_9_out, ~In[0], ~In[2]);  // AND_Gate
  and and_10 (and_10_out, In[1], ~In[0]);  // AND_Gate
  and and_11 (and_11_out, In[2], ~In[1]);  // AND_Gate
  and and_12 (and_12_out, ~In[1], ~In[0]);  // AND_Gate
  and and_13 (and_13_out, In[2], ~In[0]);  // AND_Gate
  and and_14 (and_14_out, In[1], ~In[2]);  // AND_Gate
  and and_15 (and_15_out, In[2], ~In[1]);  // AND_Gate
  and and_16 (and_16_out, In[2], ~In[0]);  // AND_Gate
  or or_1 (a, and_1_out, and_2_out, In[1]);
  or or_2 (b, ~In[2], and_3_out, and_4_out);  // OR_Gate
  or or_3 (c, In[2], In[0], ~In[1]);  // OR_Gate
  or or_4 (d, and_5_out, and_6_out, and_7_out, and_8_out);
  or or_5 (e, and_9_out, and_10_out);
  or or_6 (f, and_11_out, and_12_out, and_13_out);
  or or_7 (g, and_14_out, and_15_out, and_16_out);
endmodule

module Octal_Bin (
  input  _7,
  input  _6,
  input  _5,
  input  _4,
  input  _3,
  input  _2,
  input  _1,
  input  _0,
  output [2:0] out_9
);

  or or_1 (out_9[2], _4, _5, _6, _7);
  or or_2 (out_9[1], _2, _3, _6, _7);
  or or_3 (out_9[0], _1, _3, _5, _7);
endmodule

// OctalBinEnable
module Octal_Bin_enable (
  input  _7,
  input  _6,
  input  _5,
  input  _4,
  input  _3,
  input  _2,
  input  _1,
  input  _0,
  output Enable,
  output [2:0] Bin
);

  or or_1 (Enable, _7, _6, _5, _4, _3, _2, _1, _0);
  Octal_Bin octal_bin_1 (._7(_7), ._6(_6), ._5(_5), ._4(_4), ._3(_3), ._2(_2), ._1(_1), ._0(_0), .out_9(Bin));
endmodule
